# Fritzing sketch SchematicsSketch (saved by Fritzing 0.9.4)
breadboards: 1

parts:
  Part1 = Arduino Uno (Rev3) - ICSP
  U1 = TRANSISTOR_NPN_2 [package=to-92]
  LED1 = LED - 5mm [color="Red (633nm)" package="5 mm [THT]"]
  LED2 = LED - 5mm [color="Orange (612nm)" package="5 mm [THT]"]
  LED3 = LED - 5mm [color="Green (560nm)" package="5 mm [THT]"]
  HYGROSENSOR = mystery part, 4 pins [chip_label=Hygrometer]  # not connected

nets:
  N1: Part1.D4, LED3.anode
  N2: Part1.D5_PWM, LED2.anode
  N3: Part1.D6_PWM, LED1.anode
  N4: Part1.5V, U1.E
  N5: Part1.GND, LED1.cathode, LED2.cathode, LED3.cathode
